// Logisim project Contador_1.circ as structural Verilog: 1 circuit, main circuit contador
module contador (
  input  RESET
);

  wire and_1_out, and_2_out, and_3_out, and_4_out, and_5_out, clock_1_out, d_ff_1_q, d_ff_1_qn, d_ff_2_q,
       d_ff_2_qn, d_ff_3_q, d_ff_3_qn, not_1_out, or_1_out, xor_1_out;

  Clock clock_1 (.out(clock_1_out));
  D_Flip_Flop d_ff_1 (.D(d_ff_1_qn), .clk(clock_1_out), .Q(d_ff_1_q), .Qn(d_ff_1_qn), .reset(RESET));  // open: preset
  xor xor_1 (xor_1_out, d_ff_1_q, d_ff_2_q);
  D_Flip_Flop d_ff_2 (.D(xor_1_out), .clk(clock_1_out), .Q(d_ff_2_q), .Qn(d_ff_2_qn), .reset(RESET));  // open: preset
  and and_1 (and_1_out, d_ff_3_q, d_ff_1_qn);
  and and_2 (and_2_out, d_ff_3_q, d_ff_2_qn);
  and and_3 (and_3_out, d_ff_3_qn, d_ff_2_q, d_ff_1_q);
  or or_1 (or_1_out, and_1_out, and_2_out, and_3_out);
  D_Flip_Flop d_ff_3 (.D(or_1_out), .clk(clock_1_out), .Q(d_ff_3_q), .Qn(d_ff_3_qn), .reset(RESET));  // open: preset
  and and_4 (and_4_out, d_ff_3_q, d_ff_2_q, d_ff_1_q);
  LED led_1 (.in(and_4_out));
  and and_5 (and_5_out, d_ff_1_q, not_1_out);
  LED led_2 (.in(and_5_out));
  not not_1 (not_1_out, d_ff_3_q);
endmodule
