// Logisim project SERDES.circ as structural Verilog: 7 circuits, main circuit main
module main (
);

  wire button_1_out, button_2_out, button_3_out, button_4_out, button_5_out, button_6_out, button_7_out,
       button_8_out, button_9_out, clock_1_out, decodificador_1_a, decodificador_1_b, decodificador_1_c,
       decodificador_1_d, decodificador_1_e, decodificador_1_f, decodificador_1_g, deserealizacion_1_bit0,
       deserealizacion_1_bit1, deserealizacion_1_bit2, deserealizacion_1_bit3, dipswitch_1_sw1,
       estados_1_aout, estados_1_bout, estados_1_c0, estados_1_c1, estados_1_c2, estados_1_c3,
       estados_1_cout, estados_1_synchronize, serializacion_1_memory1, serializacion_1_memory2,
       serializacion_1_memory3, serializacion_1_memory4, serializacion_1_signal1,
       serializacion_1_synchronizes, teclado_matricial_1_aout, teclado_matricial_1_bout,
       teclado_matricial_1_cout;

  Button button_1 (.out(button_1_out));
  Button button_2 (.out(button_2_out));
  Button button_3 (.out(button_3_out));
  Button button_4 (.out(button_4_out));
  Button button_5 (.out(button_5_out));
  Button button_6 (.out(button_6_out));
  Button button_7 (.out(button_7_out));
  Button button_8 (.out(button_8_out));
  Button button_9 (.out(button_9_out));
  DipSwitch #(.number(2)) dipswitch_1 (.sw1(dipswitch_1_sw1));  // open: sw2
  Clock clock_1 (.out(clock_1_out));
  teclado_matricial teclado_matricial_1 (
    .Ain(estados_1_aout), .Bin(estados_1_bout), .Cin(estados_1_cout), .T3(button_5_out), .T2(button_4_out),
    .T1(button_1_out), .T6(button_7_out), .T5(button_6_out), .T4(button_2_out), .T9(button_9_out),
    .T8(button_8_out), .T7(button_3_out), .Aout(teclado_matricial_1_aout), .Bout(teclado_matricial_1_bout),
    .Cout(teclado_matricial_1_cout));
  Estados estados_1 (
    .init(dipswitch_1_sw1), .clock(clock_1_out), .Ain(teclado_matricial_1_aout),
    .Bin(teclado_matricial_1_bout), .Cin(teclado_matricial_1_cout), .Aout(estados_1_aout),
    .Bout(estados_1_bout), .Cout(estados_1_cout), .C0(estados_1_c0), .C1(estados_1_c1), .C2(estados_1_c2),
    .C3(estados_1_c3), .Synchronize(estados_1_synchronize));
  Serializacion serializacion_1 (
    .bit0(estados_1_c0), .bit1(estados_1_c1), .bit2(estados_1_c2), .bit3(estados_1_c3),
    .in_5(estados_1_synchronize), .Signal1(serializacion_1_signal1),
    .synchronizes(serializacion_1_synchronizes), .memory1(serializacion_1_memory1),
    .memory2(serializacion_1_memory2), .memory3(serializacion_1_memory3), .memory4(serializacion_1_memory4));
  LED led_1 (.in(serializacion_1_memory4));
  LED led_2 (.in(serializacion_1_memory3));
  LED led_3 (.in(serializacion_1_memory2));
  LED led_4 (.in(serializacion_1_memory1));
  Deserealizacion deserealizacion_1 (
    .segnal(serializacion_1_signal1), .clock(serializacion_1_synchronizes), .bit0(deserealizacion_1_bit0),
    .bit1(deserealizacion_1_bit1), .bit2(deserealizacion_1_bit2), .bit3(deserealizacion_1_bit3));
  Decodificador decodificador_1 (
    .bit3(deserealizacion_1_bit0), .bit2(deserealizacion_1_bit1), .bit1(deserealizacion_1_bit2),
    .bit0(deserealizacion_1_bit3), .a(decodificador_1_a), .b(decodificador_1_b), .c(decodificador_1_c),
    .d(decodificador_1_d), .e(decodificador_1_e), .f(decodificador_1_f), .g(decodificador_1_g));
  _7_Segment_Display u_7_segment_display_1 (
    .g(decodificador_1_g), .f(decodificador_1_f), .a(decodificador_1_a), .b(decodificador_1_b),
    .e(decodificador_1_e), .d(decodificador_1_d), .c(decodificador_1_c));  // open: dp
endmodule

module teclado_matricial (
  input  Ain,
  input  Bin,
  input  Cin,
  input  T3,
  input  T2,
  input  T1,
  input  T6,
  input  T5,
  input  T4,
  input  T9,
  input  T8,
  input  T7,
  output Aout,
  output Bout,
  output Cout
);

  wire and_1_out, and_2_out, and_3_out, and_4_out, and_5_out, and_6_out, and_7_out, and_8_out, and_9_out;

  and and_1 (and_1_out, T1, Ain);
  and and_2 (and_2_out, T4, Ain);
  and and_3 (and_3_out, T7, Ain);
  and and_4 (and_4_out, T2, Bin);
  and and_5 (and_5_out, T5, Bin);
  and and_6 (and_6_out, T8, Bin);
  and and_7 (and_7_out, T3, Cin);
  and and_8 (and_8_out, T6, Cin);
  and and_9 (and_9_out, T9, Cin);
  or or_1 (Aout, and_7_out, and_4_out, and_1_out);
  or or_2 (Bout, and_8_out, and_5_out, and_2_out);
  or or_3 (Cout, and_9_out, and_6_out, and_3_out);
endmodule

module Estados (
  input  init,
  input  clock,
  input  Ain,
  input  Bin,
  input  Cin,
  output Aout,
  output Bout,
  output Cout,
  output C0,
  output C1,
  output C2,
  output C3,
  output Synchronize
);

  wire and_7_out, and_8_out, and_9_out, and_10_out, and_11_out, and_12_out, and_13_out, and_14_out,
       and_15_out, Error, or_1_out, or_2_out, or_3_out, or_4_out, or_5_out, or_6_out, or_7_out, S1, S2, S3,
       S4, S5, S6, S7, S8, S9, xor_1_out, xor_2_out;

  xor xor_1 (xor_1_out, 1'b1, init);
  and and_1 (S1, Aout, Ain);
  and and_2 (S4, Aout, Bin);
  and and_3 (S7, Aout, Cin);
  D_Flip_Flop d_ff_1 (.D(Cout), .clk(xor_2_out), .Q(Aout), .preset(xor_1_out));  // open: Qn, reset
  and and_4 (S2, Bout, Ain);
  and and_5 (S5, Bout, Bin);
  and and_6 (S8, Bout, Cin);
  and and_7 (and_7_out, S1, S4);
  and and_8 (and_8_out, S1, S7);
  and and_9 (and_9_out, S4, S7);
  and and_10 (and_10_out, S2, S5);
  and and_11 (and_11_out, S2, S8);
  and and_12 (and_12_out, S5, S8);
  and and_13 (and_13_out, S3, S6);
  and and_14 (and_14_out, S3, S9);
  and and_15 (and_15_out, S6, S9);
  D_Flip_Flop d_ff_2 (.D(Aout), .clk(xor_2_out), .Q(Bout), .reset(xor_1_out));  // open: Qn, preset
  and and_16 (S3, Cout, Ain);
  and and_17 (S6, Cout, Bin);
  and and_18 (S9, Cout, Cin);
  D_Flip_Flop d_ff_3 (.D(Bout), .clk(xor_2_out), .Q(Cout), .reset(xor_1_out));  // open: Qn, preset
  or or_1 (or_1_out, and_7_out, and_8_out, and_9_out, and_10_out, and_11_out);
  or or_2 (or_2_out, and_12_out, and_13_out, and_14_out, and_15_out);
  xor xor_2 (xor_2_out, or_3_out, clock);
  or or_3 (or_3_out, or_4_out, or_5_out, or_6_out, or_7_out);
  nor nor_1 (Error, or_1_out, or_2_out);
  or or_4 (or_4_out, S8, S9);
  and and_19 (C3, or_4_out, Error);
  or or_5 (or_5_out, S4, S5, S6, S7);
  and and_20 (C2, or_5_out, Error);
  or or_6 (or_6_out, S2, S3, S6, S7);
  and and_21 (C1, or_6_out, Error);
  and and_22 (C0, or_7_out, Error);
  or or_7 (or_7_out, S1, S3, S5, S7, S9);

  assign Synchronize = clock;
endmodule

module Serializacion (
  input  bit0,
  input  bit1,
  input  bit2,
  input  bit3,
  input  in_5,
  output Signal1,
  output synchronizes,
  output memory1,
  output memory2,
  output memory3,
  output memory4
);

  wire and_1_out, and_2_out, and_3_out, and_4_out, and_5_out, and_6_out, and_7_out, and_8_out, and_9_out,
       and_10_out, d_ff_1_q, d_ff_1_qn, nand_1_out, not_1_out, not_2_out, not_3_out, not_4_out, not_5_out,
       or_1_out, or_2_out, S1, S2, S3;

  or or_1 (or_1_out, bit0, bit1, bit2, bit3);
  and and_1 (and_1_out, or_1_out, in_5);
  D_Flip_Flop d_ff_1 (.D(d_ff_1_qn), .Q(d_ff_1_q), .Qn(d_ff_1_qn), .preset(and_1_out));  // open: clk, reset
  D_Flip_Flop d_ff_2 (.D(bit0), .clk(and_1_out), .Q(memory1));  // open: Qn, preset, reset
  D_Flip_Flop d_ff_3 (.D(bit1), .clk(and_1_out), .Q(memory2));  // open: Qn, preset, reset
  D_Flip_Flop d_ff_4 (.D(bit2), .clk(and_1_out), .Q(memory3));  // open: Qn, preset, reset
  D_Flip_Flop d_ff_5 (.D(bit3), .clk(and_1_out), .Q(memory4));  // open: Qn, preset, reset
  and and_2 (and_2_out, not_1_out, 1'b1);
  not not_1 (not_1_out, d_ff_1_q);
  or or_2 (or_2_out, and_2_out, and_3_out);
  and and_3 (and_3_out, d_ff_1_q, nand_1_out);
  and and_4 (and_4_out, in_5, or_2_out);
  nand nand_1 (nand_1_out, S2, not_2_out, S3);
  not not_2 (not_2_out, S1);
  not not_3 (not_3_out, S1);
  not not_4 (not_4_out, S2);
  not not_5 (not_5_out, S3);
  Contador contador_1 (.Clock(and_4_out), .RESET(and_1_out), .bit0(S1), .bit1(S2), .bit2(S3));
  and and_5 (and_5_out, not_3_out, not_4_out, not_5_out, 1'b1);
  and and_6 (and_6_out, not_5_out, not_4_out, S1, memory1);
  and and_7 (and_7_out, S2, not_3_out, not_5_out, memory2);
  and and_8 (and_8_out, S2, S1, not_5_out, memory3);
  and and_9 (and_9_out, S3, not_3_out, not_4_out, memory4);
  and and_10 (and_10_out, S3, not_3_out, S2, 1'b0);
  or or_3 (Signal1, and_5_out, and_6_out, and_7_out, and_8_out, and_9_out, and_10_out);

  assign synchronizes = in_5;

  // Other names for the same wires on the sheet: CLOCK = in_5
endmodule

module Contador (
  input  Clock,
  input  RESET,
  output bit0,
  output bit1,
  output bit2
);

  wire and_1_out, and_2_out, and_3_out, d_ff_1_qn, d_ff_2_qn, d_ff_3_qn, or_1_out, xor_1_out;

  D_Flip_Flop d_ff_1 (.D(d_ff_1_qn), .clk(Clock), .Q(bit0), .Qn(d_ff_1_qn), .reset(RESET));  // open: preset
  xor xor_1 (xor_1_out, bit0, bit1);
  D_Flip_Flop d_ff_2 (.D(xor_1_out), .clk(Clock), .Q(bit1), .Qn(d_ff_2_qn), .reset(RESET));  // open: preset
  and and_1 (and_1_out, bit2, d_ff_1_qn);
  and and_2 (and_2_out, bit2, d_ff_2_qn);
  and and_3 (and_3_out, d_ff_3_qn, bit1, bit0);
  or or_1 (or_1_out, and_1_out, and_2_out, and_3_out);
  D_Flip_Flop d_ff_3 (.D(or_1_out), .clk(Clock), .Q(bit2), .Qn(d_ff_3_qn), .reset(RESET));  // open: preset
endmodule

module Deserealizacion (
  input  segnal,
  input  clock,
  output bit0,
  output bit1,
  output bit2,
  output bit3
);

  wire and_1_out, d_ff_1_q, d_ff_1_qn, d_ff_2_q, d_ff_3_q, d_ff_6_q, d_ff_7_q, d_ff_10_q;

  D_Flip_Flop d_ff_1 (.D(segnal), .clk(clock), .Q(d_ff_1_q), .Qn(d_ff_1_qn), .reset(and_1_out));  // open: preset
  D_Flip_Flop d_ff_2 (.D(d_ff_1_q), .clk(clock), .Q(d_ff_2_q), .reset(and_1_out));  // open: Qn, preset
  and and_1 (and_1_out, d_ff_1_qn, d_ff_10_q);
  D_Flip_Flop d_ff_3 (.D(d_ff_2_q), .clk(clock), .Q(d_ff_3_q), .reset(and_1_out));  // open: Qn, preset
  D_Flip_Flop d_ff_4 (.D(d_ff_2_q), .clk(and_1_out), .Q(bit3));  // open: Qn, preset, reset
  D_Flip_Flop d_ff_5 (.D(d_ff_3_q), .clk(and_1_out), .Q(bit2));  // open: Qn, preset, reset
  D_Flip_Flop d_ff_6 (.D(d_ff_3_q), .clk(clock), .Q(d_ff_6_q), .reset(and_1_out));  // open: Qn, preset
  D_Flip_Flop d_ff_7 (.D(d_ff_6_q), .clk(clock), .Q(d_ff_7_q), .reset(and_1_out));  // open: Qn, preset
  D_Flip_Flop d_ff_8 (.D(d_ff_6_q), .clk(and_1_out), .Q(bit1));  // open: Qn, preset, reset
  D_Flip_Flop d_ff_9 (.D(d_ff_7_q), .clk(and_1_out), .Q(bit0));  // open: Qn, preset, reset
  D_Flip_Flop d_ff_10 (.D(d_ff_7_q), .clk(clock), .Q(d_ff_10_q), .reset(and_1_out));  // open: Qn, preset
endmodule

module Decodificador (
  input  bit3,
  input  bit2,
  input  bit1,
  input  bit0,
  output a,
  output b,
  output c,
  output d,
  output e,
  output f,
  output g
);

  wire and_1_out, and_2_out, and_3_out, and_4_out, and_5_out, and_6_out, and_7_out, and_8_out, and_9_out,
       and_10_out, and_11_out, and_12_out, and_13_out, and_14_out, and_15_out, and_16_out, and_17_out,
       and_18_out, and_19_out, and_20_out, and_21_out, and_22_out, and_23_out, and_24_out, and_25_out,
       and_26_out, and_27_out, and_28_out, and_29_out, and_30_out, and_31_out, and_32_out, and_33_out,
       and_34_out, and_35_out, and_36_out, and_37_out, and_38_out, and_39_out, and_40_out, not_1_out,
       not_2_out, not_3_out, not_4_out;

  not not_1 (not_1_out, bit0);
  not not_2 (not_2_out, bit1);
  not not_3 (not_3_out, bit2);
  not not_4 (not_4_out, bit3);
  and and_1 (and_1_out, not_2_out, not_4_out);
  and and_2 (and_2_out, not_1_out, bit2);
  and and_3 (and_3_out, not_1_out, bit1, bit3);
  and and_4 (and_4_out, bit0, not_2_out, not_3_out);
  and and_5 (and_5_out, bit0, not_4_out);
  and and_6 (and_6_out, bit1, bit2);
  and and_7 (and_7_out, not_1_out, not_3_out, not_4_out);
  and and_8 (and_8_out, not_1_out, bit2, bit3);
  and and_9 (and_9_out, not_2_out, not_4_out);
  and and_10 (and_10_out, bit0, not_3_out, bit3);
  and and_11 (and_11_out, not_1_out, not_2_out);
  and and_12 (and_12_out, not_1_out, bit1);
  and and_13 (and_13_out, bit0, not_2_out);
  and and_14 (and_14_out, not_3_out, bit3);
  and and_15 (and_15_out, not_1_out, not_3_out);
  and and_16 (and_16_out, not_1_out, bit3);
  and and_17 (and_17_out, bit1, not_3_out, bit3);
  and and_18 (and_18_out, not_1_out, not_2_out, not_4_out);
  and and_19 (and_19_out, not_1_out, not_2_out, bit2);
  and and_20 (and_20_out, not_1_out, bit2, not_4_out);
  and and_21 (and_21_out, not_2_out, not_3_out, not_4_out);
  and and_22 (and_22_out, bit0, not_3_out);
  and and_23 (and_23_out, not_2_out, bit2, bit3);
  and and_24 (and_24_out, bit1, bit2, not_4_out);
  and and_25 (and_25_out, not_2_out, not_4_out);
  and and_26 (and_26_out, bit2, not_4_out);
  and and_27 (and_27_out, bit0, bit2);
  and and_28 (and_28_out, bit0, bit1);
  and and_29 (and_29_out, not_3_out, not_4_out);
  and and_30 (and_30_out, not_1_out, bit1, not_3_out);
  and and_31 (and_31_out, bit1, not_4_out);
  and and_32 (and_32_out, bit0, not_2_out);
  and and_33 (and_33_out, bit0, bit2);
  and and_34 (and_34_out, not_2_out, bit2);
  and and_35 (and_35_out, bit0, not_2_out);
  and and_36 (and_36_out, not_1_out, bit1, not_3_out);
  and and_37 (and_37_out, not_1_out, bit1, not_4_out);
  and and_38 (and_38_out, bit1, not_3_out, bit3);
  and and_39 (and_39_out, bit2, not_4_out);
  and and_40 (and_40_out, bit0, bit3);
  or or_1 (a, and_1_out, and_2_out, and_3_out, and_4_out, and_5_out, and_6_out);
  or or_2 (b, and_7_out, and_8_out, and_9_out, and_10_out, and_11_out);
  or or_3 (c, and_12_out, and_13_out, and_14_out, and_15_out, and_16_out);
  or or_4 (d, and_17_out, and_18_out, and_19_out, and_20_out, and_21_out, and_22_out, and_23_out, and_24_out);
  or or_5 (e, and_25_out, and_26_out, and_27_out, and_28_out);
  or or_6 (f, and_29_out, and_30_out, and_31_out, and_32_out, and_33_out);
  or or_7 (g, and_34_out, and_35_out, and_36_out, and_37_out, and_38_out, and_39_out, and_40_out);
endmodule
